# Fritzing sketch layout (saved by Fritzing 0.9.2b)
breadboards: 1

parts:
  Part1 = Arduino Uno (Rev3)
  R1 = Resistor [tolerance=±5% resistance=220 package="2010 [SMD]"]
  S1 = Reed switch [package=THT]

nets:
  N1: Part1.D4, R1.Pin_0, S1.pin_1
  N2: Part1.3V3, S1.pin_2
  N3: Part1.GND, R1.Pin_1

notes:
  Need a BLE shield connected.
